# Fritzing sketch main (saved by Fritzing 0.9.4)

parts:
  SparkFun_74HC4051_8-Channel_Mux_Breakout2 = SparkFun-74HC4051-8-Channel-Mux-Breakout [part_number=BOB-13906]
  U2 = Beetle Micro USB ATMEGA32U4 [package=dip]
  SW1 = Rotary_encoder [package=encoder_led_3]
  SW2 = Rotary_encoder [package=encoder_led_3]
  SW3 = Rotary_encoder [package=encoder_led_3]
  U4 = Slide_potentiometer_10k [package=slider]
  U5 = Slide_potentiometer_10k [package=slider]
  U6 = Slide_potentiometer_10k [package=slider]

nets:
  N1: SparkFun_74HC4051_8-Channel_Mux_Breakout2.Y7, SW1.CLK
  N2: SparkFun_74HC4051_8-Channel_Mux_Breakout2.Y6, SW1.DT
  N3: SparkFun_74HC4051_8-Channel_Mux_Breakout2.Y5, SW1.SW
  N4: SparkFun_74HC4051_8-Channel_Mux_Breakout2.Y4, SW2.CLK
  N5: SparkFun_74HC4051_8-Channel_Mux_Breakout2.Y3, SW2.DT
  N6: SparkFun_74HC4051_8-Channel_Mux_Breakout2.Y2, SW2.SW
  N7: SparkFun_74HC4051_8-Channel_Mux_Breakout2.S2, U2.D11
  N8: SparkFun_74HC4051_8-Channel_Mux_Breakout2.S1, U2.D10
  N9: SparkFun_74HC4051_8-Channel_Mux_Breakout2.S0, U2.D9
  N10: SparkFun_74HC4051_8-Channel_Mux_Breakout2.Z, U2.DX
  GND: SparkFun_74HC4051_8-Channel_Mux_Breakout2.GND, U2.GND
  VCC: SparkFun_74HC4051_8-Channel_Mux_Breakout2.VCC, U2.5V
  N11: U2.A0, U4.OTB
  N12: U2.A1, U5.OTB
  N13: U2.A2, U6.OTB
  VCC_2: SW1.+, SW2.+, SW3.+, U4.VCC, U5.VCC, U6.VCC
  GND_2: SW1.GND, SW2.GND, SW3.GND, U4.GND, U5.GND, U6.GND

custom parts:
  Beetle Micro USB ATMEGA32U4: Beetle Micro USB ATMEGA32U4 Module Mini Development Expansion Board For Arduino Leonardo R3 DC 5V I2C IIC UART Interface from Aliexpress
  Rotary_encoder: 360 Degrees Rotary Encoder Module For Arduino
  Slide_potentiometer_10k: Slide Potentiometer 10K Linear Module Dual Output for Arduino AVR Electronic Block
